// Digital circuit register-file.dig as structural Verilog
module register_file (
  input  [4:0] ReadReg1,
  input  [4:0] ReadReg2,
  input  [4:0] WriteReg,
  input  [31:0] WriteData,
  input  RegWrite,
  input  Clock,
  output [31:0] ReadData1,
  output [31:0] ReadData2
);

  wire R0, R1, R2, R3, R4, R5, R6, R7, R8, R9, R10, R11, R12, R13, R14, R15, R16, R17, R18, R19, R20, R21,
       R22, R23, R24, R25, R26, R27, R28, R29, R30, R31;
  wire [4:0] bitextender_1_out, WR;
  wire [31:0] O0, O1, O2, O3, O4, O5, O6, O7, O8, O9, O10, O11, O12, O13, O14, O15, O16, O17, O18, O19, O20,
       O21, O22, O23, O24, O25, O26, O27, O28, O29, O30, O31;

  Register #(.Bits(32)) Reg_0 (.D({32{1'b0}}), .C(Clock), .en(R0), .Q(O0));
  Register #(.Bits(32)) Reg_9 (.D(WriteData), .C(Clock), .en(R9), .Q(O9));
  Register #(.Bits(32)) Reg_18 (.D(WriteData), .C(Clock), .en(R18), .Q(O18));
  Register #(.Bits(32)) Reg_27 (.D(WriteData), .C(Clock), .en(R27), .Q(O27));
  BitExtender #(.inputBits(1), .outputBits(5)) bitextender_1 (.in(RegWrite), .out(bitextender_1_out));
  Register #(.Bits(32)) Reg_1 (.D(WriteData), .C(Clock), .en(R1), .Q(O1));
  Register #(.Bits(32)) Reg_10 (.D(WriteData), .C(Clock), .en(R10), .Q(O10));
  Decoder #(.Selector_Bits(5)) decoder_1 (
    .sel(WR), .out_0(R0), .out_1(R1), .out_2(R2), .out_3(R3), .out_4(R4), .out_5(R5), .out_6(R6), .out_7(R7),
    .out_8(R8), .out_9(R9), .out_10(R10), .out_11(R11), .out_12(R12), .out_13(R13), .out_14(R14),
    .out_15(R15), .out_16(R16), .out_17(R17), .out_18(R18), .out_19(R19), .out_20(R20), .out_21(R21),
    .out_22(R22), .out_23(R23), .out_24(R24), .out_25(R25), .out_26(R26), .out_27(R27), .out_28(R28),
    .out_29(R29), .out_30(R30), .out_31(R31));
  Register #(.Bits(32)) Reg_19 (.D(WriteData), .C(Clock), .en(R19), .Q(O19));
  Register #(.Bits(32)) Reg_28 (.D(WriteData), .C(Clock), .en(R28), .Q(O28));
  assign WR = WriteReg & bitextender_1_out;  // And and_1, 5 bits wide
  Register #(.Bits(32)) Reg_2 (.D(WriteData), .C(Clock), .en(R2), .Q(O2));
  Register #(.Bits(32)) Reg_11 (.D(WriteData), .C(Clock), .en(R11), .Q(O11));
  Register #(.Bits(32)) Reg_20 (.D(WriteData), .C(Clock), .en(R20), .Q(O20));
  Register #(.Bits(32)) Reg_29 (.D(WriteData), .C(Clock), .en(R29), .Q(O29));
  Register #(.Bits(32)) Reg_3 (.D(WriteData), .C(Clock), .en(R3), .Q(O3));
  Register #(.Bits(32)) Reg_12 (.D(WriteData), .C(Clock), .en(R12), .Q(O12));
  Register #(.Bits(32)) Reg_21 (.D(WriteData), .C(Clock), .en(R21), .Q(O21));
  Register #(.Bits(32)) Reg_30 (.D(WriteData), .C(Clock), .en(R30), .Q(O30));
  Multiplexer #(.Selector_Bits(5), .Bits(32)) multiplexer_1 (
    .sel(ReadReg1), .in_0(O0), .in_1(O1), .in_2(O2), .in_3(O3), .in_4(O4), .in_5(O5), .in_6(O6), .in_7(O7),
    .in_8(O8), .in_9(O9), .in_10(O10), .in_11(O11), .in_12(O12), .in_13(O13), .in_14(O14), .in_15(O15),
    .in_16(O16), .in_17(O17), .in_18(O18), .in_19(O19), .in_20(O20), .in_21(O21), .in_22(O22), .in_23(O23),
    .in_24(O24), .in_25(O25), .in_26(O26), .in_27(O27), .in_28(O28), .in_29(O29), .in_30(O30), .in_31(O31),
    .out(ReadData1));
  Multiplexer #(.Selector_Bits(5), .Bits(32)) multiplexer_2 (
    .sel(ReadReg2), .in_0(O0), .in_1(O1), .in_2(O2), .in_3(O3), .in_4(O4), .in_5(O5), .in_6(O6), .in_7(O7),
    .in_8(O8), .in_9(O9), .in_10(O10), .in_11(O11), .in_12(O12), .in_13(O13), .in_14(O14), .in_15(O15),
    .in_16(O16), .in_17(O17), .in_18(O18), .in_19(O19), .in_20(O20), .in_21(O21), .in_22(O22), .in_23(O23),
    .in_24(O24), .in_25(O25), .in_26(O26), .in_27(O27), .in_28(O28), .in_29(O29), .in_30(O30), .in_31(O31),
    .out(ReadData2));
  Register #(.Bits(32)) Reg_4 (.D(WriteData), .C(Clock), .en(R4), .Q(O4));
  Register #(.Bits(32)) Reg_13 (.D(WriteData), .C(Clock), .en(R13), .Q(O13));
  Register #(.Bits(32)) Reg_22 (.D(WriteData), .C(Clock), .en(R22), .Q(O22));
  Register #(.Bits(32)) Reg_31 (.D(WriteData), .C(Clock), .en(R31), .Q(O31));
  Register #(.Bits(32)) Reg_5 (.D(WriteData), .C(Clock), .en(R5), .Q(O5));
  Register #(.Bits(32)) Reg_14 (.D(WriteData), .C(Clock), .en(R14), .Q(O14));
  Register #(.Bits(32)) Reg_23 (.D(WriteData), .C(Clock), .en(R23), .Q(O23));
  Register #(.Bits(32)) Reg_6 (.D(WriteData), .C(Clock), .en(R6), .Q(O6));
  Register #(.Bits(32)) Reg_15 (.D(WriteData), .C(Clock), .en(R15), .Q(O15));
  Register #(.Bits(32)) Reg_24 (.D(WriteData), .C(Clock), .en(R24), .Q(O24));
  Register #(.Bits(32)) Reg_7 (.D(WriteData), .C(Clock), .en(R7), .Q(O7));
  Register #(.Bits(32)) Reg_16 (.D(WriteData), .C(Clock), .en(R16), .Q(O16));
  Register #(.Bits(32)) Reg_25 (.D(WriteData), .C(Clock), .en(R25), .Q(O25));
  Register #(.Bits(32)) Reg_8 (.D(WriteData), .C(Clock), .en(R8), .Q(O8));
  Register #(.Bits(32)) Reg_17 (.D(WriteData), .C(Clock), .en(R17), .Q(O17));
  Register #(.Bits(32)) Reg_26 (.D(WriteData), .C(Clock), .en(R26), .Q(O26));

  // Other names for the same wires on the sheet: C = Clock; RD1[31:0] = ReadData1; RD2[31:0] = ReadData2;
  //   Read1[4:0] = ReadReg1; Read2[4:0] = ReadReg2; WD[31:0] = WriteData
endmodule

/* Test case Register File Test:
WriteReg WriteData RegWrite Clock ReadReg1 ReadReg2 ReadData1 ReadData2

# $1 = 25
1 25 1 C 1 0 25 0

# $2 = 30
2 30 1 C 0 2 0 30

# $(N+1) = (N+1)
loop(N, 30)
	(N+1) (N+1) 1 C (N+1) (N) (N+1) (N)
end loop

# $(N+1) = N-60
loop(N, 30)
	(N+1) (N-60) 1 C (N+1) (N+1) (N-60) (N-60)
end loop

# Try writing to $0. This should not write anything
0 25 1 C 0 0 0 0

# try writing when RegWrite = 0
# (the registers should still have their old values)
loop(N, 30)
	(N+1) (N+80) 0 C (N+1) (N+1) (N-60) (N-60)
end loop
*/
